// Logisim project ALUs.circ as structural Verilog: 9 circuits, main circuit main
module main (
  input  [2:0] in_1,
  input  [7:0] A,
  input  [7:0] A_2,
  output [7:0] Salida,
  output desbordamiento
);

  ALU5 alu5_1 (
    .A0(A[0]), .B0(A_2[0]), .A1(A[1]), .B1(A_2[1]), .A2(A[2]), .B2(A_2[2]), .A3(A[3]), .B3(A_2[3]),
    .A4(A[4]), .B4(A_2[4]), .A5(A[5]), .B5(A_2[5]), .A6(A[6]), .B6(A_2[6]), .A7(A[7]), .B7(A_2[7]),
    .in_1(in_1), .out_26(desbordamiento), .S0(Salida[0]), .S1(Salida[1]), .S2(Salida[2]), .S3(Salida[3]),
    .S4(Salida[4]), .S5(Salida[5]), .S6(Salida[6]), .S7(Salida[7]));

  // Notes on the sheet:
  //   000-AND
  //   001-OR
  //   010-NOR
  //   011-igualdad
  //   100-suma
  //   101-resta
endmodule

module \xor  (
  input  A,
  input  B,
  output S
);

  wire and_1_out, and_2_out, not_1_out, not_2_out;

  not not_1 (not_1_out, A);
  not not_2 (not_2_out, B);
  and and_1 (and_1_out, A, not_2_out);
  and and_2 (and_2_out, not_1_out, B);
  or or_1 (S, and_1_out, and_2_out);
endmodule

module sum (
  input  in,
  input  A,
  input  B,
  output S,
  output out
);

  wire and_1_out, and_2_out, xor_1_s;

  \xor  xor_1 (.A(A), .B(B), .S(xor_1_s));
  \xor  xor_2 (.A(in), .B(xor_1_s), .S(S));
  and and_1 (and_1_out, in, xor_1_s);
  and and_2 (and_2_out, A, B);
  or or_1 (out, and_1_out, and_2_out);

  // Notes on the sheet:
  //   Sumador de 1 bit
endmodule

module ALU1 (
  input  Cin,
  input  [2:0] Op,
  input  A,
  input  B,
  output out_5,
  output Cout
);

  wire and_1_out, or_1_out, sum_1_s;

  and and_1 (and_1_out, A, B);
  or or_1 (or_1_out, A, B);
  sum sum_1 (.A(A), .B(B), .in(Cin), .S(sum_1_s), .out(Cout));
  Multiplexer #(.select(3), .enable("false")) multiplexer_1 (
    .in0(and_1_out), .in1(or_1_out), .in2(1'b0), .in3(1'b0), .in4(sum_1_s), .in5(1'b0), .in6(1'b0),
    .in7(1'b0), .out(out_5), .sel(Op));

  // Notes on the sheet:
  //   ALU de 1 bit con suma, and y or
endmodule

module ALU2 (
  input  [2:0] in_1,
  input  A0,
  input  B0,
  input  A1,
  input  B1,
  input  A2,
  input  B2,
  input  A3,
  input  B3,
  input  A4,
  input  B4,
  input  A5,
  input  B5,
  input  A6,
  input  B6,
  input  A7,
  input  B7,
  output S0,
  output S1,
  output S2,
  output S3,
  output S4,
  output S5,
  output S6,
  output S7,
  output out_26
);

  wire alu1_1_cout, alu1_2_cout, alu1_3_cout, alu1_4_cout, alu1_5_cout, alu1_6_cout, alu1_7_cout,
       alu1_8_cout, not_1_out, not_2_out;

  ALU1 alu1_1 (.A(A0), .B(B0), .Cin(1'b0), .Op(in_1), .Cout(alu1_1_cout), .out_5(S0));
  ALU1 alu1_2 (.A(A1), .B(B1), .Cin(alu1_1_cout), .Op(in_1), .Cout(alu1_2_cout), .out_5(S1));
  ALU1 alu1_3 (.A(A2), .B(B2), .Cin(alu1_2_cout), .Op(in_1), .Cout(alu1_3_cout), .out_5(S2));
  ALU1 alu1_4 (.A(A3), .B(B3), .Cin(alu1_3_cout), .Op(in_1), .Cout(alu1_4_cout), .out_5(S3));
  ALU1 alu1_5 (.A(A4), .B(B4), .Cin(alu1_4_cout), .Op(in_1), .Cout(alu1_5_cout), .out_5(S4));
  ALU1 alu1_6 (.A(A5), .B(B5), .Cin(alu1_5_cout), .Op(in_1), .Cout(alu1_6_cout), .out_5(S5));
  ALU1 alu1_7 (.A(A6), .B(B6), .Cin(alu1_6_cout), .Op(in_1), .Cout(alu1_7_cout), .out_5(S6));
  ALU1 alu1_8 (.A(A7), .B(B7), .Cin(alu1_7_cout), .Op(in_1), .Cout(alu1_8_cout), .out_5(S7));
  and and_1 (out_26, alu1_8_cout, in_1[2], not_2_out, not_1_out);
  not not_1 (not_1_out, in_1[0]);
  not not_2 (not_2_out, in_1[1]);

  // Notes on the sheet:
  //   000-AND
  //   001-OR
  //   100-suma
  //   ALU 8 bits con suma, and y or.
endmodule

module ALU3 (
  input  [2:0] Op,
  input  Cin,
  input  A,
  input  B,
  output out_5,
  output Cout
);

  wire and_1_out, and_2_out, not_1_out, not_2_out, or_1_out, sum_1_s, xor_1_s, xor_2_s;

  \xor  xor_1 (.A(and_1_out), .B(B), .S(xor_1_s));
  and and_1 (and_1_out, Op[0], not_1_out, Op[2]);
  not not_1 (not_1_out, Op[1]);
  and and_2 (and_2_out, A, xor_1_s);
  or or_1 (or_1_out, A, xor_1_s);
  sum sum_1 (.A(A), .B(xor_1_s), .in(Cin), .S(sum_1_s), .out(Cout));
  \xor  xor_2 (.A(A), .B(xor_1_s), .S(xor_2_s));
  not not_2 (not_2_out, xor_2_s);
  Multiplexer #(.select(3), .enable("false")) multiplexer_1 (
    .in0(and_2_out), .in1(or_1_out), .in2(1'b0), .in3(not_2_out), .in4(sum_1_s), .in5(sum_1_s), .in6(1'b0),
    .in7(1'b0), .out(out_5), .sel(Op));

  // Notes on the sheet:
  //   ALU de 1 bit con and, or, suma y resta
endmodule

module ALU4 (
  input  [2:0] in_1,
  input  A0,
  input  B0,
  input  A1,
  input  B1,
  input  A2,
  input  B2,
  input  A3,
  input  B3,
  input  A4,
  input  B4,
  input  A5,
  input  B5,
  input  A6,
  input  B6,
  input  A7,
  input  B7,
  output S0,
  output S1,
  output S2,
  output S3,
  output S4,
  output S5,
  output S6,
  output S7,
  output out_26
);

  wire alu3_1_cout, alu3_2_cout, alu3_3_cout, alu3_4_cout, alu3_5_cout, alu3_6_cout, alu3_7_cout,
       alu3_8_cout, and_1_out, not_1_out, not_2_out, not_3_out;

  and and_1 (and_1_out, in_1[0], not_1_out, in_1[2]);
  not not_1 (not_1_out, in_1[1]);
  ALU3 alu3_1 (.A(A0), .B(B0), .Cin(and_1_out), .Op(in_1), .Cout(alu3_1_cout), .out_5(S0));
  ALU3 alu3_2 (.A(A1), .B(B1), .Cin(alu3_1_cout), .Op(in_1), .Cout(alu3_2_cout), .out_5(S1));
  ALU3 alu3_3 (.A(A2), .B(B2), .Cin(alu3_2_cout), .Op(in_1), .Cout(alu3_3_cout), .out_5(S2));
  ALU3 alu3_4 (.A(A3), .B(B3), .Cin(alu3_3_cout), .Op(in_1), .Cout(alu3_4_cout), .out_5(S3));
  ALU3 alu3_5 (.A(A4), .B(B4), .Cin(alu3_4_cout), .Op(in_1), .Cout(alu3_5_cout), .out_5(S4));
  ALU3 alu3_6 (.A(A5), .B(B5), .Cin(alu3_5_cout), .Op(in_1), .Cout(alu3_6_cout), .out_5(S5));
  ALU3 alu3_7 (.A(A6), .B(B6), .Cin(alu3_6_cout), .Op(in_1), .Cout(alu3_7_cout), .out_5(S6));
  ALU3 alu3_8 (.A(A7), .B(B7), .Cin(alu3_7_cout), .Op(in_1), .Cout(alu3_8_cout), .out_5(S7));
  not not_2 (not_2_out, in_1[0]);
  not not_3 (not_3_out, in_1[1]);
  and and_2 (out_26, alu3_8_cout, in_1[2], not_3_out, not_2_out);

  // Notes on the sheet:
  //   000-AND
  //   001-OR
  //   011-igualdad
  //   100-suma
  //   101-resta
  //   ALU de 8 bits con suma, resta, and, or, igualdad
endmodule

module alunor (
  input  [2:0] Op,
  input  Cin,
  input  A,
  input  B,
  output out_5,
  output Cout
);

  wire and_1_out, and_2_out, not_1_out, not_2_out, not_3_out, or_1_out, sum_1_s, xor_1_s, xor_2_s;

  \xor  xor_1 (.A(and_1_out), .B(B), .S(xor_1_s));
  and and_1 (and_1_out, Op[0], not_1_out, Op[2]);
  not not_1 (not_1_out, Op[1]);
  and and_2 (and_2_out, A, xor_1_s);
  or or_1 (or_1_out, A, xor_1_s);
  sum sum_1 (.A(A), .B(xor_1_s), .in(Cin), .S(sum_1_s), .out(Cout));
  \xor  xor_2 (.A(A), .B(xor_1_s), .S(xor_2_s));
  not not_2 (not_2_out, or_1_out);
  not not_3 (not_3_out, xor_2_s);
  Multiplexer #(.select(3), .enable("false")) multiplexer_1 (
    .in0(and_2_out), .in1(or_1_out), .in2(not_2_out), .in3(not_3_out), .in4(sum_1_s), .in5(sum_1_s),
    .in6(1'b0), .in7(1'b0), .out(out_5), .sel(Op));
endmodule

module ALU5 (
  input  [2:0] in_1,
  input  A0,
  input  B0,
  input  A1,
  input  B1,
  input  A2,
  input  B2,
  input  A3,
  input  B3,
  input  A4,
  input  B4,
  input  A5,
  input  B5,
  input  A6,
  input  B6,
  input  A7,
  input  B7,
  output S0,
  output S1,
  output S2,
  output S3,
  output S4,
  output S5,
  output S6,
  output S7,
  output out_26
);

  wire alunor_1_cout, alunor_2_cout, alunor_3_cout, alunor_4_cout, alunor_5_cout, alunor_6_cout,
       alunor_7_cout, alunor_8_cout, and_1_out, not_1_out, not_2_out, not_3_out;

  and and_1 (and_1_out, in_1[0], not_1_out, in_1[2]);
  not not_1 (not_1_out, in_1[1]);
  alunor alunor_1 (.A(A0), .B(B0), .Cin(and_1_out), .Op(in_1), .Cout(alunor_1_cout), .out_5(S0));
  alunor alunor_2 (.A(A1), .B(B1), .Cin(alunor_1_cout), .Op(in_1), .Cout(alunor_2_cout), .out_5(S1));
  alunor alunor_3 (.A(A2), .B(B2), .Cin(alunor_2_cout), .Op(in_1), .Cout(alunor_3_cout), .out_5(S2));
  alunor alunor_4 (.A(A3), .B(B3), .Cin(alunor_3_cout), .Op(in_1), .Cout(alunor_4_cout), .out_5(S3));
  alunor alunor_5 (.A(A4), .B(B4), .Cin(alunor_4_cout), .Op(in_1), .Cout(alunor_5_cout), .out_5(S4));
  alunor alunor_6 (.A(A5), .B(B5), .Cin(alunor_5_cout), .Op(in_1), .Cout(alunor_6_cout), .out_5(S5));
  alunor alunor_7 (.A(A6), .B(B6), .Cin(alunor_6_cout), .Op(in_1), .Cout(alunor_7_cout), .out_5(S6));
  alunor alunor_8 (.A(A7), .B(B7), .Cin(alunor_7_cout), .Op(in_1), .Cout(alunor_8_cout), .out_5(S7));
  not not_2 (not_2_out, in_1[0]);
  not not_3 (not_3_out, in_1[1]);
  and and_2 (out_26, alunor_8_cout, in_1[2], not_3_out, not_2_out);

  // Notes on the sheet:
  //   000-AND
  //   001-OR
  //   010-NOR
  //   011-igualdad
  //   100-suma
  //   101-resta
  //   ALU de 8 bits con suma, resta, and, or, igualdad y nor
endmodule
